# Fritzing sketch sketch (saved by Fritzing 0.9.3b)
breadboards: 1

parts:
  Mod1 = Arduino MKR Wifi 1010
  LED1 = smd LED [color="Red (633nm)" package="0805 [SMD]"]

nets:
  N1: Mod1.D6, LED1.anode
  N2: Mod1.GND, LED1.cathode

custom parts:
  Arduino MKR Wifi 1010: Arduino MKR Wifi 1010, SAMD21 Cortex-M0+ 32bit Low Power ARM MCU,Flash Memory 256 KB, SRAM 32KB, 48mhz clock, Ublok Wifi interface.
